// Digital circuit alu.dig as structural Verilog
module alu (
  input  [7:0] A,
  input  [7:0] B,
  input  [3:0] Opcode,
  output [7:0] O
);

  wire [7:0] add_1_s, and_1_out, div_1_q, mul_1_mul, not_1_out, or_1_out, sub_1_s, xor_1_out;
  wire [15:8] mul_1_mul_2;

  Add #(.Bits(8)) add_1 (.a(A), .b(B), .c_i(1'b0), .s(add_1_s));  // open: c_o
  Sub #(.Bits(8)) sub_1 (.a(A), .b(B), .c_i(1'b0), .s(sub_1_s));  // open: c_o
  Mul #(.Bits(8)) mul_1 (.a(A), .b(B), .mul({mul_1_mul_2, mul_1_mul}));
  Div #(.Bits(8)) div_1 (.a(A), .b(B), .q(div_1_q));  // open: r
  assign not_1_out = ~A;  // Not not_1, 8 bits wide
  assign and_1_out = A & B;  // And and_1, 8 bits wide
  assign or_1_out = A | B;  // Or or_1, 8 bits wide
  assign xor_1_out = A ^ B;  // XOr xor_1, 8 bits wide
  Multiplexer #(.Selector_Bits(3), .Bits(8)) multiplexer_1 (
    .sel(Opcode[2:0]), .in_0(add_1_s), .in_1(sub_1_s), .in_2(mul_1_mul), .in_3(div_1_q), .in_4(not_1_out),
    .in_5(and_1_out), .in_6(or_1_out), .in_7(xor_1_out), .out(O));
endmodule
