// Digital circuit decoder.dig as structural Verilog
module decoder (
  input  [19:0] Inst,
  output [3:0] Opcode,
  output [3:0] Reg_1,
  output [3:0] Reg_2,
  output [7:0] Val_IMMPTR
);


  assign Opcode = Inst[19:16];
  assign Reg_1 = Inst[15:12];
  assign Reg_2 = Inst[11:8];
  assign Val_IMMPTR = Inst[7:0];

  // Notes on the sheet:
  //   Inst: Raw Instruction Bytes
endmodule
