// Digital circuit exec.dig as structural Verilog
module exec (
  input  [3:0] Opcode,
  input  [7:0] Da_RF,
  input  [7:0] Db_RF,
  input  [3:0] Reg_1,
  input  [3:0] Reg_2,
  input  [7:0] Val_IMMPTR,
  input  [7:0] Q_RAM,
  input  [7:0] O_ALU,
  output [7:0] A_ALU,
  output [7:0] B_ALU,
  output [7:0] Din_RF,
  output [3:0] RW_RF,
  output WE_RF,
  output [7:0] A_RAM,
  output [7:0] D_RAM,
  output WE_RAM,
  output PC_Override,
  output [7:0] PC_OverrideVal,
  output HLT_Flag
);

  wire comparator_1_eq, not_1_out;

  Comparator #(.Bits(8)) comparator_1 (.a(Da_RF), .b({8{1'b0}}), .eq(comparator_1_eq));  // open: gt, lt
  not not_1 (not_1_out, comparator_1_eq);
  Multiplexer #(.Selector_Bits(4)) multiplexer_1 (
    .sel(Opcode), .in_0(1'b0), .in_1(1'b0), .in_2(1'b0), .in_3(1'b0), .in_4(1'b0), .in_5(1'b1),
    .in_6(comparator_1_eq), .in_7(not_1_out), .in_8(1'b0), .in_9(1'b0), .in_10(1'b0), .in_11(1'b0),
    .in_12(1'b0), .in_13(1'b0), .in_14(1'b0), .in_15(1'b0), .out(PC_Override));
  Multiplexer #(.Selector_Bits(4), .Bits(8)) multiplexer_2 (
    .sel(Opcode), .in_0({8{1'b0}}), .in_1(Val_IMMPTR), .in_2(Q_RAM), .in_3({8{1'b0}}), .in_4(Db_RF),
    .in_5({8{1'b0}}), .in_6({8{1'b0}}), .in_7({8{1'b0}}), .in_8(O_ALU), .in_9(O_ALU), .in_10(O_ALU),
    .in_11(O_ALU), .in_12(O_ALU), .in_13(O_ALU), .in_14(O_ALU), .in_15(O_ALU), .out(Din_RF));
  Multiplexer #(.Selector_Bits(4)) multiplexer_3 (
    .sel(Opcode), .in_0(1'b0), .in_1(1'b1), .in_2(1'b1), .in_3(1'b0), .in_4(1'b1), .in_5(1'b0), .in_6(1'b0),
    .in_7(1'b0), .in_8(1'b1), .in_9(1'b1), .in_10(1'b1), .in_11(1'b1), .in_12(1'b1), .in_13(1'b1),
    .in_14(1'b1), .in_15(1'b1), .out(WE_RF));
  Multiplexer #(.Selector_Bits(4), .Bits(4)) multiplexer_4 (
    .sel(Opcode), .in_0(4'b0000), .in_1(Reg_1), .in_2(Reg_1), .in_3(4'b0000), .in_4(Reg_1), .in_5(4'b0000),
    .in_6(4'b0000), .in_7(4'b0000), .in_8(Reg_1), .in_9(Reg_1), .in_10(Reg_1), .in_11(Reg_1), .in_12(Reg_1),
    .in_13(Reg_1), .in_14(Reg_1), .in_15(Reg_1), .out(RW_RF));
  Comparator #(.Bits(4)) comparator_2 (.a(Opcode), .b(4'b0000), .eq(HLT_Flag));  // open: gt, lt
  Multiplexer #(.Selector_Bits(4), .Bits(8)) multiplexer_5 (
    .sel(Opcode), .in_0({8{1'b0}}), .in_1({8{1'b0}}), .in_2(Val_IMMPTR), .in_3(Val_IMMPTR), .in_4({8{1'b0}}),
    .in_5({8{1'b0}}), .in_6({8{1'b0}}), .in_7({8{1'b0}}), .in_8({8{1'b0}}), .in_9({8{1'b0}}),
    .in_10({8{1'b0}}), .in_11({8{1'b0}}), .in_12({8{1'b0}}), .in_13({8{1'b0}}), .in_14({8{1'b0}}),
    .in_15({8{1'b0}}), .out(A_RAM));
  Multiplexer #(.Selector_Bits(4), .Bits(8)) multiplexer_6 (
    .sel(Opcode), .in_0({8{1'b0}}), .in_1({8{1'b0}}), .in_2({8{1'b0}}), .in_3(Da_RF), .in_4({8{1'b0}}),
    .in_5({8{1'b0}}), .in_6({8{1'b0}}), .in_7({8{1'b0}}), .in_8({8{1'b0}}), .in_9({8{1'b0}}),
    .in_10({8{1'b0}}), .in_11({8{1'b0}}), .in_12({8{1'b0}}), .in_13({8{1'b0}}), .in_14({8{1'b0}}),
    .in_15({8{1'b0}}), .out(D_RAM));
  Multiplexer #(.Selector_Bits(4)) multiplexer_7 (
    .sel(Opcode), .in_0(1'b0), .in_1(1'b0), .in_2(1'b0), .in_3(1'b1), .in_4(1'b0), .in_5(1'b0), .in_6(1'b0),
    .in_7(1'b0), .in_8(1'b0), .in_9(1'b0), .in_10(1'b0), .in_11(1'b0), .in_12(1'b0), .in_13(1'b0),
    .in_14(1'b0), .in_15(1'b0), .out(WE_RAM));

  assign A_ALU = Da_RF;
  assign B_ALU = Db_RF;
  assign PC_OverrideVal = Val_IMMPTR;

  // Notes on the sheet:
  //   Din_RF: Data
  //   RW_RF: Register Write Dest
endmodule
