// Digital circuit p8.dig as structural Verilog
module p8 (
  input  clk,
  output Overflow,
  output [7:0] out_2,
  output [7:0] out_3,
  output [7:0] out_4
);

  wire and_2_out, Clk_2, Clk_t, d_ff_1_q, decoder_1_mode, exec_1_pc_override, exec_1_we_ram, exec_1_we_rf,
       HLT_Flag, not_1_out;
  wire [2:0] exec_1_ra_rf, exec_1_rb_rf, exec_1_rw_rf, Reg_1, Reg_2;
  wire [4:0] decoder_1_opcode;
  wire [7:0] exec_1_a_alu, exec_1_a_ram, exec_1_b_alu, exec_1_d_ram, exec_1_din_rf, exec_1_pc_overrideval,
       ramasync_1_q, registerfile_1_da, registerfile_1_db;
  wire [19:0] Instruction_Memory_d;

  ROM #(.AddrBits(8), .isProgramMemory("true"), .Bits(20)) Instruction_Memory (
    .A(out_2), .sel(1'b1), .D(Instruction_Memory_d));
  decoder decoder_1 (
    .Inst(Instruction_Memory_d), .Opcode(decoder_1_opcode), .Reg_1(Reg_1), .Reg_2(Reg_2), .Val_IMMPTR(out_3),
    .Mode(decoder_1_mode));
  D_FF d_ff_1 (.D(Clk_t), .C(Clk_t), .Q(d_ff_1_q));  // open: nQ
  CounterPreset #(.Bits(8), .isProgramCounter("true")) counterpreset_1 (
    .en(1'b1), .C(Clk_2), .dir(1'b0), .in(exec_1_pc_overrideval), .ld(exec_1_pc_override), .clr(1'b0),
    .out(out_2), .ovf(Overflow));
  and and_1 (Clk_2, not_1_out, d_ff_1_q);
  not not_1 (not_1_out, Clk_t);
  or or_1 (Clk_t, clk, HLT_Flag);
  RegisterFile #(.AddrBits(3), .Bits(8)) registerfile_1 (
    .Din(exec_1_din_rf), .we(exec_1_we_rf), .Rw(exec_1_rw_rf), .C(Clk_t), .Ra(exec_1_ra_rf),
    .Rb(exec_1_rb_rf), .Da(registerfile_1_da), .Db(registerfile_1_db));
  RAMAsync #(.AddrBits(8), .Bits(8)) ramasync_1 (.A(exec_1_a_ram), .D(exec_1_d_ram), .we(and_2_out), .Q(ramasync_1_q));
  exec exec_1 (
    .Opcode(decoder_1_opcode), .Da_RF(registerfile_1_da), .Db_RF(registerfile_1_db), .Reg_1(Reg_1),
    .Reg_2(Reg_2), .Val_IMMPTR(out_3), .Q_RAM(ramasync_1_q), .O_ALU(out_4), .Mode(decoder_1_mode),
    .A_ALU(exec_1_a_alu), .Din_RF(exec_1_din_rf), .RW_RF(exec_1_rw_rf), .WE_RF(exec_1_we_rf),
    .A_RAM(exec_1_a_ram), .D_RAM(exec_1_d_ram), .WE_RAM(exec_1_we_ram), .PC_Override(exec_1_pc_override),
    .PC_OverrideVal(exec_1_pc_overrideval), .HLT_Flag(HLT_Flag), .Ra_RF(exec_1_ra_rf), .Rb_RF(exec_1_rb_rf),
    .B_ALU(exec_1_b_alu));
  and and_2 (and_2_out, exec_1_we_ram, Clk_t);
  alu alu_1 (.A(exec_1_a_alu), .B(exec_1_b_alu), .Opcode(decoder_1_opcode), .O(out_4));

  // Other names for the same wires on the sheet: PC[7:0] = out_2

  // Notes on the sheet:
  //   clk: Hz: 10
  //   contents of Instruction_Memory (hex, n*v repeats v):
  //   9015,a029,e9401,3800c,50010,30014,8001,30018,8003,30018,8005,30018,f8000
endmodule
